# Fritzing sketch Arduino (saved by Fritzing 1.0.6)
breadboards: 3

parts:
  Grove1 = Grove OLED 128x96
  S4 = Pushbutton [package="[THT]"]
  S1 = Pushbutton [package="[THT]"]
  S2 = Pushbutton [package="[THT]"]
  S3 = Pushbutton [package="[THT]"]
  Pro_Micro1 = Pro Micro
  Pro_Micro2 = Pro Micro
  S7 = Pushbutton [package="[THT]"]

nets:
  N1: Grove1.GND, Pro_Micro1.GND#23
  VCC: Grove1.VCC, Pro_Micro1.VCC
  N2: Grove1.SDA, Pro_Micro1.D2
  N3: Grove1.SCL, Pro_Micro1.D3
  N4: S4.Pin_1, S4.Pin_2, Pro_Micro1.D5
  N5: S4.Pin_3, S4.Pin_4, S1.Pin_3, S1.Pin_4, S2.Pin_3, S2.Pin_4, S3.Pin_3, S3.Pin_4, Pro_Micro1.GND#3
  N6: S1.Pin_1, S1.Pin_2, Pro_Micro1.D8
  N7: S2.Pin_1, S2.Pin_2, Pro_Micro1.D7
  N8: S3.Pin_1, S3.Pin_2, Pro_Micro1.D6
  N9: Pro_Micro2.GND, S7.Pin_3, S7.Pin_4
  N10: Pro_Micro2.D5, S7.Pin_1, S7.Pin_2

custom parts:
  Pro Micro: The SparkFun Pro Micro is a complete USB-based microcontoller development system, in a very small footprint, capable of implementing many types of projects. All programming can be done via the USB port.
